# Fritzing sketch Bluetooth-HC06 (saved by Fritzing 1.0.4)
breadboards: 1

parts:
  Part1 = Bluetooth HC-05 Macho
  R1 = Resistor [tolerance=±5% resistance=2.2k package="0603 [SMD]"]
  R2 = Resistor [tolerance=±5% resistance=1k package="0805 [SMD]"]
  Part2 = Arduino Uno (Rev3)
  Resistor = Resistor [tolerance=±5% resistance=1k package="0603 [SMD]"]  # not connected
  Resistor_2 = Resistor [tolerance=±5% resistance=2.2k package="0603 [SMD]"]  # not connected

nets:
  N1: Part1.TXD, Part2.D2
  N2: Part1.RXD, R1.Pin_1, R2.Pin_1
  VCC: Part1.VCC, Part2.5V
  GND: Part1.GND, R1.Pin_0, Part2.GND
  N3: R2.Pin_0, Part2.D3_PWM
